# Fritzing sketch weihnacht (saved by Fritzing 1.0.2b)
breadboards: 1

parts:
  R1 = Slide Potentiometer [maximum_resistance=22k knob_status=50% power=0.5W]
  R2 = Slide Potentiometer [maximum_resistance=22kΩ knob_status=50% power=0.5W]
  R3 = Slide Potentiometer [maximum_resistance=22kΩ knob_status=50% power=0.5W]
  BD139 = NPN-Transistor [package="TO92 [THT]"]
  BD139_2 = NPN-Transistor [package="TO92 [THT]"]
  BD139_3 = NPN-Transistor [package="TO92 [THT]"]
  U1 = Vibration Motor- ROB-08449 [package=vibe-motor-10mm]
  18xRGB = LED - 5mm [color="Red (633nm)" current=0.030A package="5 mm [THT]"]
  37xRGB = LED - 5mm [color="Red (633nm)" current=0.030A package="5 mm [THT]"]
  U1_2 = ATTiny84 [package=dip]
  R7 = Resistor [tolerance=±5% resistance=10k power=0.25W package=THT]
  R8 = Resistor [tolerance=±5% resistance=10k power=0.25W package=THT]
  S1 = Pushbutton [package=THT]
  S2 = Pushbutton [package=THT]
  C1 = Ceramic Capacitor [capacitance=100nF package="100 mil [THT, multilayer]"]
  C2 = Electrolytic Capacitor [capacitance=4.7µF package="100 mil [THT, electrolytic]"]
  C3 = Electrolytic Capacitor [capacitance=10µF voltage=35V package="100 mil [THT, electrolytic]"]
  R9 = Resistor [tolerance=±5% power=0.25W resistance=220 package=THT]
  R4 = Resistor [tolerance=±5% power=0.25W resistance=330 package=THT]
  R5 = Resistor [tolerance=±5% power=0.25W resistance=330 package=THT]
  R6 = Resistor [tolerance=±5% power=0.25W resistance=330 package=THT]
  S3 = Pushbutton [package=THT]
  J1 = Screw terminal - 2 pins [package=THT]

nets:
  GND: R1.leg1, R2.leg1, R3.leg1, BD139_2.E, U1.-, 18xRGB.anode, U1_2.pin14, S1.leg0, S2.leg0, C1.0, C2.-, C3.-, C3.+, S3.leg0, J1.pin2
  N1: R1.wiper, U1_2.pin10
  N2: R1.leg2, R2.leg2, R3.leg2, BD139.C, BD139_2.C, BD139_3.C, U1_2.pin1, R7.Pin_0, R8.Pin_0, C1.1, R9.Pin_0
  N3: R2.wiper, U1_2.pin12
  N4: R3.wiper, U1_2.pin11
  N5: BD139.E, U1.+
  N6: BD139.B, R6.Pin_1
  N7: BD139_2.B, R5.Pin_1
  N8: BD139_3.B, R4.Pin_1
  N9: 37xRGB.anode, C2.+
  N10: U1_2.pin2, R7.Pin_1, S1.leg1
  N11: U1_2.pin3, R8.Pin_1, S2.leg1
  N12: U1_2.pin5, R4.Pin_0
  N13: U1_2.pin6, R5.Pin_0
  N14: U1_2.pin7, R6.Pin_0
  N15: U1_2.pin8, R9.Pin_1, S3.leg1
  N16: U1_2.pin9, J1.pin1

notes:
  ATTiny84
  Baum
  Grund
  T1
  T2
  T3
  Motor
  Test
  M1
  M2
  M3
  M4
  M5
  M6

custom parts:
  ATTiny84: Atmel ATTiny84 processor. 8 ADC pins, 4 PWM pins. Available in either 10MHz or 20MHz. The last 2 pin numbers refer to arduino. D6 = Arduino 6, A6 = Arduino A6 example: PA6 (SDA/MOSI/OC1A/DI/AD6/PCINT6/D6/A6) NOTE: This part is diagrammed to suit the MIT HLT ATTiny84 core at https://github.com/damellis/attiny/
